# Fritzing sketch uart_connection (saved by Fritzing 0.9.10b)

parts:
  Heltec_Wireless_Stick1 = Heltec Wireless Stick [part_number=HTIT-WS]
  U1 = LuaNode32 / ESP32 [part_number=ESP32S-PIN30]

nets:
  N1: Heltec_Wireless_Stick1.pin_14, U1.TX2
  N2: Heltec_Wireless_Stick1.pin_30, U1.RX2

custom parts:
  Heltec Wireless Stick: Wireless Stick is a part of the Heltec LoRa series and incorporates an ESP32 processor, WiFi, SX1276 LoRa and Bluetooth with an integrated CP2102 USB to serial port interface and onboard SHT1.25 battery interface with integrated lithium battery management system.
  LuaNode32 / ESP32: New Image for LuaNode32 DOIT ESP32 DEVKIT V1. Base parts from LuaNode32 / ESP32 ESP32 based LuaNode32 by G.Noorlander DOIT Esp32 DevKit v1 (30 pins long, 11 pins width) by Werner Rothschopf (modified by vanepp Dec 2018)
